# Fritzing sketch sound-booster (saved by Fritzing 0.9.3b)
circuit board: 8.46667cm x 5.64444cm
breadboards: 1

parts:
  C1 = Electrolytic Capacitor [capacitance=100µF voltage=50V package="100 mil [THT, electrolytic]"]
  Q1 = NPN-Transistor [package="TO92 [THT]"]
  R2 = Resistor [tolerance=±5% resistance=1k package=THT]
  LED1 = LED - 5mm [color="Infrared (850nm)" package="5 mm [THT]"]
  Part1 = Arduino Uno (Rev3)
  PART1 = Sound Detector
  R1 = Rotary Potentiometer (Small) [maximum_resistance=100kΩ package=THT]

nets:
  GND: C1.-, Q1.E, Part1.GND, PART1.GND, R1.leg2
  5V: C1.+, LED1.anode, Part1.5V, PART1.VCC, R1.leg1
  N1: Q1.B, R2.Pin_0
  N2: Q1.C, LED1.cathode
  N3: R2.Pin_1, Part1.D3_PWM
  N4: Part1.A0, PART1.ENVELOPE
  N5: Part1.A1, R1.wiper

custom parts:
  Sound Detector: Electret microphone with multiple outputs. - First output is the actual audio - Second output is the amplitude envelope - Third output is a binary "sound present" indication - high while sound is present, low otherwise. Visit sparkfun.com for more documentations.
